// Logisim project zaid.circ as structural Verilog: 5 circuits, main circuit main
module main (
  input  in_1,
  input  in_2,
  input  in_3,
  output [5:0] out_4,
  output out_5,
  output [4:0] out_6,
  output [31:0] out_7,
  output [4:0] out_8,
  output [4:0] out_9
);

  wire clock_1_out;
  wire [31:0] adder_1_out, register_1_q, rom_1_data;

  Register #(.width(32)) register_1 (.D(adder_1_out), .en(in_1), .Q(register_1_q), .clk(clock_1_out), .clr(in_2));
  Clock clock_1 (.out(clock_1_out));
  // Probe on register_1_q
  Adder #(.width(32)) adder_1 (.a(register_1_q), .b(32'h4), .out(adder_1_out));  // open: cin, cout
  // Probe on rom_1_data
  ROM #(.addrWidth(24), .dataWidth(32)) rom_1 (.addr(register_1_q[25:2]), .data(rom_1_data), .sel(in_3));
  Control_Decoder control_decoder_1 (
    ._32bit_instruction(rom_1_data), .rd(out_6), .rs1(out_9), .rs2(out_8), ._32bit_immediate(out_7),
    .aluOP(out_4), .regWrite(out_5));

  // Notes on the sheet:
  //   contents of rom_1 (hex, n*v repeats v):
  //   11000011 11000001 10111011 1101001 1100110 10001010 10011001 1010101
endmodule

module decoder (
  input  [31:0] _32_bit_instructions,
  output [6:0] opcode,
  output [4:0] rd,
  output [2:0] func_3,
  output [4:0] rs1,
  output [4:0] rs2,
  output [6:0] func_7
);


  assign func_3 = _32_bit_instructions[14:12];
  assign func_7 = _32_bit_instructions[31:25];
  assign opcode = _32_bit_instructions[6:0];
  assign rd = _32_bit_instructions[11:7];
  assign rs1 = _32_bit_instructions[19:15];
  assign rs2 = _32_bit_instructions[24:20];
endmodule

module Control_Unit (
  input  [6:0] in_1,
  input  [2:0] in_2,
  input  [1:0] in_3,
  output [5:0] alu_op,
  output regWrite
);

  wire and_1_out, and_2_out, and_3_out, and_4_out, and_5_out, and_6_out, comparator_1_eq, comparator_2_eq,
       comparator_3_eq, comparator_4_eq, comparator_5_eq, comparator_6_eq, comparator_7_eq, comparator_8_eq,
       comparator_9_eq, comparator_10_eq, comparator_13_eq, comparator_14_eq, comparator_15_eq,
       comparator_16_eq, comparator_17_eq, demultiplexer_1_out0, demultiplexer_1_out1, demultiplexer_1_out2,
       demultiplexer_1_out3, demultiplexer_1_out4, demultiplexer_1_out5, demultiplexer_1_out7,
       demultiplexer_1_out8, demultiplexer_2_out0, demultiplexer_2_out1, demultiplexer_2_out2,
       demultiplexer_2_out3, demultiplexer_2_out4, demultiplexer_3_out0, demultiplexer_3_out1,
       demultiplexer_3_out2, demultiplexer_4_out0, demultiplexer_4_out1, demultiplexer_4_out2,
       demultiplexer_4_out3, demultiplexer_4_out4, demultiplexer_4_out5, demultiplexer_4_out7,
       demultiplexer_4_out8, demultiplexer_5_out0, demultiplexer_5_out1, demultiplexer_5_out4,
       demultiplexer_5_out5, demultiplexer_5_out6, demultiplexer_5_out7, demultiplexer_6_out0,
       demultiplexer_6_out1, demultiplexer_7_out0, demultiplexer_7_out1, demultiplexer_8_out0,
       demultiplexer_8_out1, not_1_out, or_1_out;
  wire [2:0] bge;
  wire [4:0] add, multiplexer_1_out;

  Comparator #(.width(7)) comparator_1 (.a(7'b0010011), .b(in_1), .eq(comparator_1_eq));  // open: gt, lt
  Demultiplexer #(.select(4), .enable("false")) demultiplexer_1 (
    .out0(demultiplexer_1_out0), .out1(demultiplexer_1_out1), .out2(demultiplexer_1_out2),
    .out3(demultiplexer_1_out3), .out4(demultiplexer_1_out4), .out5(demultiplexer_1_out5),
    .out6(demultiplexer_1_out5), .out7(demultiplexer_1_out7), .out8(demultiplexer_1_out8),
    .in(comparator_1_eq), .sel({1'b0, in_2}));  // open: out9, out10, out11, out12, out13, out14, out15
  Comparator #(.width(7)) comparator_2 (.a(7'b0110011), .b(in_1), .eq(comparator_2_eq));  // open: gt, lt
  Comparator #(.width(7)) comparator_3 (.a(7'b1100011), .b(in_1), .eq(comparator_3_eq));  // open: gt, lt
  Demultiplexer #(.select(3), .enable("false")) demultiplexer_2 (
    .out0(demultiplexer_2_out0), .out1(demultiplexer_2_out1), .out2(demultiplexer_2_out2),
    .out3(demultiplexer_2_out3), .out4(demultiplexer_2_out4), .in(comparator_4_eq), .sel(in_2));  // open: out5, out6, out7
  Comparator #(.width(7)) comparator_4 (.a(7'b0000011), .b(in_1), .eq(comparator_4_eq));  // open: gt, lt
  Comparator #(.width(7)) comparator_5 (.a(7'b0100011), .b(in_1), .eq(comparator_5_eq));  // open: gt, lt
  Demultiplexer #(.select(2), .enable("false")) demultiplexer_3 (
    .out0(demultiplexer_3_out0), .out1(demultiplexer_3_out1), .out2(demultiplexer_3_out2),
    .in(comparator_5_eq), .sel(in_2[1:0]));  // open: out3
  Demultiplexer #(.select(4), .enable("false")) demultiplexer_4 (
    .out0(demultiplexer_4_out0), .out1(demultiplexer_4_out1), .out2(demultiplexer_4_out2),
    .out3(demultiplexer_4_out3), .out4(demultiplexer_4_out4), .out5(demultiplexer_4_out5),
    .out6(demultiplexer_4_out5), .out7(demultiplexer_4_out7), .out8(demultiplexer_4_out8),
    .in(comparator_2_eq), .sel({1'b0, in_2}));  // open: out9, out10, out11, out12, out13, out14, out15
  Demultiplexer #(.select(3), .enable("false")) demultiplexer_5 (
    .out0(demultiplexer_5_out0), .out1(demultiplexer_5_out1), .out4(demultiplexer_5_out4),
    .out5(demultiplexer_5_out5), .out6(demultiplexer_5_out6), .out7(demultiplexer_5_out7),
    .in(comparator_3_eq), .sel(in_2));  // open: out2, out3
  Comparator #(.width(7)) comparator_6 (.a(7'b1100111), .b(in_1), .eq(comparator_6_eq));  // open: gt, lt
  Comparator #(.width(7)) comparator_7 (.a(7'b1101111), .b(in_1), .eq(comparator_7_eq));  // open: gt, lt
  Comparator #(.width(7)) comparator_8 (.a(7'b0010111), .b(in_1), .eq(comparator_8_eq));  // open: gt, lt
  Comparator #(.width(7)) comparator_9 (.a(7'b0110111), .b(in_1), .eq(comparator_9_eq));  // open: gt, lt
  // Probe on 5'b00100
  // Probe on 5'b11100
  assign bge = comparator_6_eq ? 3'b011 : 3'bz;  // Controlled_Buffer controlled_buffer_1
  LED led_1 (.in(comparator_6_eq));
  assign bge = comparator_7_eq ? 3'b100 : 3'bz;  // Controlled_Buffer controlled_buffer_2
  LED led_2 (.in(comparator_7_eq));
  assign add = comparator_8_eq ? 5'b01110 : 5'bz;  // Controlled_Buffer controlled_buffer_3
  LED led_3 (.in(comparator_8_eq));
  assign add = comparator_9_eq ? 5'b11100 : 5'bz;  // Controlled_Buffer controlled_buffer_4
  LED led_4 (.in(comparator_9_eq));
  Comparator #(.width(7)) comparator_10 (.a(7'b0000011), .b(in_1), .eq(comparator_10_eq));  // open: gt, lt
  Comparator #(.width(7)) comparator_11 (.a(7'b0010011), .b(in_1), .eq(comparator_10_eq));  // open: gt, lt
  Comparator #(.width(7)) comparator_12 (.a({7{1'b1}}), .b(in_1), .eq(comparator_10_eq));  // open: gt, lt
  Comparator #(.width(7)) comparator_13 (.a(7'b0100011), .b(in_1), .eq(comparator_13_eq));  // open: gt, lt
  Comparator #(.width(7)) comparator_14 (.a(7'b1100011), .b(in_1), .eq(comparator_14_eq));  // open: gt, lt
  Comparator #(.width(7)) comparator_15 (.a(7'b0110011), .b(in_1), .eq(comparator_15_eq));  // open: gt, lt
  Comparator #(.width(7)) comparator_16 (.a(7'b1101111), .b(in_1), .eq(comparator_16_eq));  // open: gt, lt
  Comparator #(.width(7)) comparator_17 (.a(7'b0110111), .b(in_1), .eq(comparator_17_eq));  // open: gt, lt
  assign add = demultiplexer_2_out4 ? 5'b00100 : 5'bz;  // Controlled_Buffer controlled_buffer_5
  LED led_5 (.in(demultiplexer_2_out4));
  assign add = demultiplexer_3_out2 ? 5'b10001 : 5'bz;  // Controlled_Buffer controlled_buffer_6
  assign add = demultiplexer_2_out3 ? 5'b00011 : 5'bz;  // Controlled_Buffer controlled_buffer_7
  assign add = demultiplexer_2_out2 ? 5'b00010 : 5'bz;  // Controlled_Buffer controlled_buffer_8
  assign add = demultiplexer_3_out1 ? 5'b10000 : 5'bz;  // Controlled_Buffer controlled_buffer_9
  LED led_6 (.in(demultiplexer_3_out1));
  LED led_7 (.in(demultiplexer_3_out2));
  and and_1 (and_1_out, comparator_10_eq, 1'b1);
  and and_2 (and_2_out, comparator_13_eq, 1'b0);
  and and_3 (and_3_out, comparator_14_eq, 1'b0);
  and and_4 (and_4_out, comparator_15_eq, 1'b1);
  and and_5 (and_5_out, comparator_16_eq, 1'b1);
  and and_6 (and_6_out, comparator_17_eq, 1'b1);
  assign add = demultiplexer_2_out1 ? 5'b00001 : 5'bz;  // Controlled_Buffer controlled_buffer_10
  LED led_8 (.in(demultiplexer_2_out2));
  LED led_9 (.in(demultiplexer_2_out3));
  assign add = demultiplexer_3_out0 ? 5'b01111 : 5'bz;  // Controlled_Buffer controlled_buffer_11
  LED led_10 (.in(demultiplexer_3_out0));
  assign add = demultiplexer_2_out0 ? {5{1'b0}} : 5'bz;  // Controlled_Buffer controlled_buffer_12
  LED led_11 (.in(demultiplexer_2_out0));
  LED led_12 (.in(demultiplexer_2_out1));
  assign bge = demultiplexer_5_out7 ? 3'b010 : 3'bz;  // Controlled_Buffer controlled_buffer_13
  LED led_13 (.in(demultiplexer_1_out7));
  LED led_14 (.in(demultiplexer_1_out8));
  // Probe on 3'b010
  or or_1 (or_1_out, demultiplexer_5_out7, comparator_6_eq, comparator_7_eq, demultiplexer_5_out5, demultiplexer_5_out6);
  or or_2 (regWrite, and_1_out, and_2_out, and_3_out, and_4_out, and_5_out, and_6_out);
  assign bge = demultiplexer_5_out6 ? 3'b001 : 3'bz;  // Controlled_Buffer controlled_buffer_14
  assign bge = not_1_out ? 3'b101 : 3'bz;  // Controlled_Buffer controlled_buffer_15
  not not_1 (not_1_out, or_1_out);
  assign add = demultiplexer_1_out8 ? 5'b01101 : 5'bz;  // Controlled_Buffer controlled_buffer_16
  assign add = demultiplexer_1_out7 ? 5'b01100 : 5'bz;  // Controlled_Buffer controlled_buffer_17
  Demultiplexer #(.select(2), .enable("false")) demultiplexer_6 (
    .out0(demultiplexer_6_out0), .out1(demultiplexer_6_out1), .in(demultiplexer_1_out5), .sel(in_3));  // open: out2, out3
  assign bge = demultiplexer_5_out5 ? 3'b000 : 3'bz;  // Controlled_Buffer controlled_buffer_18
  assign add = demultiplexer_5_out4 ? {5{1'b1}} : 5'bz;  // Controlled_Buffer controlled_buffer_19
  LED led_15 (.in(demultiplexer_5_out7));
  assign add = demultiplexer_6_out1 ? 5'b01011 : 5'bz;  // Controlled_Buffer controlled_buffer_20
  assign add = demultiplexer_5_out1 ? 5'b11110 : 5'bz;  // Controlled_Buffer controlled_buffer_21
  LED led_16 (.in(demultiplexer_5_out5));
  LED led_17 (.in(demultiplexer_5_out6));
  assign add = demultiplexer_6_out0 ? 5'b01010 : 5'bz;  // Controlled_Buffer controlled_buffer_22
  assign add = demultiplexer_1_out4 ? 5'b01001 : 5'bz;  // Controlled_Buffer controlled_buffer_23
  LED led_18 (.in(demultiplexer_6_out0));
  LED led_19 (.in(demultiplexer_6_out1));
  assign add = demultiplexer_5_out0 ? 5'b11101 : 5'bz;  // Controlled_Buffer controlled_buffer_24
  LED led_20 (.in(demultiplexer_5_out0));
  LED led_21 (.in(demultiplexer_5_out1));
  LED led_22 (.in(demultiplexer_5_out4));
  assign add = demultiplexer_1_out3 ? 5'b01000 : 5'bz;  // Controlled_Buffer controlled_buffer_25
  assign add = demultiplexer_4_out8 ? 5'b11011 : 5'bz;  // Controlled_Buffer controlled_buffer_26
  LED led_23 (.in(demultiplexer_4_out8));
  assign add = demultiplexer_1_out2 ? 5'b00111 : 5'bz;  // Controlled_Buffer controlled_buffer_27
  assign add = demultiplexer_4_out7 ? 5'b11010 : 5'bz;  // Controlled_Buffer controlled_buffer_28
  LED led_24 (.in(demultiplexer_4_out7));
  Demultiplexer #(.select(2), .enable("false")) demultiplexer_7 (
    .out0(demultiplexer_7_out0), .out1(demultiplexer_7_out1), .in(demultiplexer_4_out5), .sel(in_3));  // open: out2, out3
  assign add = demultiplexer_1_out1 ? 5'b00110 : 5'bz;  // Controlled_Buffer controlled_buffer_29
  assign add = demultiplexer_1_out0 ? 5'b00101 : 5'bz;  // Controlled_Buffer controlled_buffer_30
  LED led_25 (.in(demultiplexer_1_out4));
  LED led_26 (.in(demultiplexer_1_out1));
  LED led_27 (.in(demultiplexer_1_out2));
  LED led_28 (.in(demultiplexer_1_out3));
  assign add = demultiplexer_7_out1 ? 5'b11001 : 5'bz;  // Controlled_Buffer controlled_buffer_31
  assign add = demultiplexer_7_out0 ? 5'b11000 : 5'bz;  // Controlled_Buffer controlled_buffer_32
  LED led_29 (.in(demultiplexer_7_out0));
  LED led_30 (.in(demultiplexer_7_out1));
  LED led_31 (.in(demultiplexer_1_out0));
  assign add = demultiplexer_4_out4 ? 5'b10111 : 5'bz;  // Controlled_Buffer controlled_buffer_33
  assign add = demultiplexer_4_out3 ? 5'b10110 : 5'bz;  // Controlled_Buffer controlled_buffer_34
  assign add = demultiplexer_4_out2 ? 5'b10101 : 5'bz;  // Controlled_Buffer controlled_buffer_35
  LED led_32 (.in(demultiplexer_4_out2));
  LED led_33 (.in(demultiplexer_4_out3));
  LED led_34 (.in(demultiplexer_4_out4));
  assign add = demultiplexer_4_out1 ? 5'b10100 : 5'bz;  // Controlled_Buffer controlled_buffer_36
  Demultiplexer #(.select(2), .enable("false")) demultiplexer_8 (
    .out0(demultiplexer_8_out0), .out1(demultiplexer_8_out1), .in(demultiplexer_4_out0), .sel(in_3));  // open: out2, out3
  LED led_35 (.in(demultiplexer_4_out1));
  assign add = demultiplexer_8_out0 ? 5'b10010 : 5'bz;  // Controlled_Buffer controlled_buffer_37
  assign add = demultiplexer_8_out1 ? 5'b10011 : 5'bz;  // Controlled_Buffer controlled_buffer_38
  LED led_36 (.in(demultiplexer_8_out1));
  LED led_37 (.in(demultiplexer_8_out0));
  Multiplexer #(.select(5), .width(5), .enable("false")) multiplexer_1 (
    .in0({5{1'b0}}), .in1(5'b00001), .in2(5'b00010), .in3(5'b00011), .in4(5'b00100), .in5(5'b00101),
    .in6(5'b00110), .in7(5'b00111), .in8(5'b01000), .in9(5'b01001), .in10(5'b01010), .in11(5'b01011),
    .in12(5'b01100), .in13(5'b01101), .in14(5'b01110), .in15(5'b01111), .in16(5'b10000), .in17(5'b10001),
    .in18(5'b10010), .in19(5'b10011), .in20(5'b10100), .in21(5'b10101), .in22(5'b10110), .in23(5'b10111),
    .in24(5'b11000), .in25(5'b11001), .in26(5'b11010), .in27(5'b11011), .in28(5'b11100), .in29(5'b11101),
    .in30(5'b11110), .in31({5{1'b1}}), .out(multiplexer_1_out), .sel(add));
  // Probe on multiplexer_1_out
  // Probe on alu_op
  Multiplexer #(.select(3), .width(6), .enable("false")) multiplexer_2 (
    .in0(6'b100000), .in1(6'b100001), .in2(6'b100010), .in3(6'b100011), .in4(6'b100100),
    .in5({1'b0, multiplexer_1_out}), .out(alu_op), .sel(bge));  // open: in6, in7

  // Other names for the same wires on the sheet: _14_12_FUNC_3[2:0] = in_2; addi[4:0] = add; and[4:0] = add;
  //   andi[4:0] = add; auipc[4:0] = add; beq[4:0] = add; blt[4:0] = add; bne[4:0] = add; lb[4:0] = add;
  //   lbu[4:0] = add; lh[4:0] = add; lhu[4:0] = add; lui[4:0] = add; lw[4:0] = add; or[4:0] = add; ori[4:0] = add;
  //   sb[4:0] = add; sh[4:0] = add; sll[4:0] = add; slli[4:0] = add; slt[4:0] = add; slti[4:0] = add;
  //   sltiu[4:0] = add; sltu[4:0] = add; sra[4:0] = add; srai[4:0] = add; srl[4:0] = add; srli[4:0] = add;
  //   sub[4:0] = add; sw[4:0] = add; xor[4:0] = add; xori[4:0] = add; bgeu[2:0] = bge; bltu[2:0] = bge; en[2:0] = bge;
  //   jal[2:0] = bge; jalr[2:0] = bge; _30_31_FUNC_7[1:0] = in_3; Opcode[6:0] = in_1

  // Notes on the sheet:
  //   alu i-type
  //   load i-type
  //   s-type
  //   r-type
  //   sb-type
  //   I-TYPE
  //   S-TYPE
  //   SB-TYPE
  //   R-TYPE
  //   UJ-TYPE
  //   U-TYPE
  //   JALR i-type
  //   JAL uj-type
  //   AUIPC u-type
  //   LUI u-type
  //   load i-type
  //   alu i-type
  //   jalr i-type
  //   store
  //   SB-type
  //   r-type
  //   jal UJ-type
  //   auipc/lui U-type
  //   WRITE REG
  //   ALU OPERATIONS
endmodule

// sw
module Control_Decoder (
  input  [31:0] _32bit_instruction,
  output regWrite,
  output [4:0] rd,
  output [4:0] rs1,
  output [4:0] rs2,
  output [5:0] aluOP,
  output [31:0] _32bit_immediate
);

  wire [2:0] decoder_1_func_3;
  wire [6:0] decoder_1_func_7, decoder_1_opcode;

  decoder decoder_1 (
    ._32_bit_instructions(_32bit_instruction), .opcode(decoder_1_opcode), .rd(rd), .func_3(decoder_1_func_3),
    .rs1(rs1), .rs2(rs2), .func_7(decoder_1_func_7));
  // Probe on decoder_1_opcode
  immediate_generation immediate_generation_1 (
    .in_1(decoder_1_opcode), .in_2(_32bit_instruction), .out_3(_32bit_immediate));
  Control_Unit control_unit_1 (
    .in_1(decoder_1_opcode), .in_2(decoder_1_func_3), .in_3(decoder_1_func_7[6:5]), .alu_op(aluOP),
    .regWrite(regWrite));
endmodule

module immediate_generation (
  input  [6:0] in_1,
  input  [31:0] in_2,
  output [31:0] out_3
);

  wire comparator_1_eq, comparator_2_eq, comparator_3_eq, comparator_4_eq, comparator_5_eq, comparator_6_eq,
       comparator_7_eq, or_1_out;
  wire [2:0] controlled_buffer_6_out;
  wire [11:0] controlled_buffer_1_out, controlled_buffer_3_out;
  wire [12:0] controlled_buffer_4_out;
  wire [20:0] controlled_buffer_2_out;
  wire [31:0] bit_extender_1_out, bit_extender_2_out, bit_extender_3_out, bit_extender_4_out,
       controlled_buffer_5_out;

  Comparator #(.width(7)) comparator_1 (.a(7'b0000011), .b(in_1), .eq(comparator_1_eq));  // open: gt, lt
  Comparator #(.width(7)) comparator_2 (.a(7'b0010011), .b(in_1), .eq(comparator_2_eq));  // open: gt, lt
  Comparator #(.width(7)) comparator_3 (.a({7{1'b1}}), .b(in_1), .eq(comparator_3_eq));  // open: gt, lt
  Comparator #(.width(7)) comparator_4 (.a(7'b0100011), .b(in_1), .eq(comparator_4_eq));  // open: gt, lt
  Comparator #(.width(7)) comparator_5 (.a(7'b1100011), .b(in_1), .eq(comparator_5_eq));  // open: gt, lt
  Comparator #(.width(7)) comparator_6 (.a(7'b1101111), .b(in_1), .eq(comparator_6_eq));  // open: gt, lt
  Comparator #(.width(7)) comparator_7 (.a(7'b0110111), .b(in_1), .eq(comparator_7_eq));  // open: gt, lt
  or or_1 (or_1_out, comparator_1_eq, comparator_2_eq, comparator_3_eq);
  // Probe on {in_2[31:25], in_2[11:7]}
  assign controlled_buffer_1_out = or_1_out ? in_2[31:20] : 12'bz;  // Controlled_Buffer controlled_buffer_1
  assign controlled_buffer_2_out = comparator_7_eq ? {in_2[31], in_2[19:12], in_2[20], in_2[30:21], 1'b0} : 21'bz;  // Controlled_Buffer controlled_buffer_2
  // Probe on controlled_buffer_1_out
  assign controlled_buffer_3_out = comparator_4_eq ? {in_2[31:25], in_2[11:7]} : 12'bz;  // Controlled_Buffer controlled_buffer_3
  // Probe on controlled_buffer_4_out
  assign controlled_buffer_4_out = comparator_5_eq ? {in_2[31], in_2[7], in_2[30:25], in_2[11:8], 1'b0} : 13'bz;  // Controlled_Buffer controlled_buffer_4
  // Probe on {in_2[31:12], {12{1'b0}}}
  assign controlled_buffer_5_out = comparator_6_eq ? {in_2[31:12], {12{1'b0}}} : 32'bz;  // Controlled_Buffer controlled_buffer_5
  assign controlled_buffer_6_out = or_1_out ? 3'b000 : 3'bz;  // Controlled_Buffer controlled_buffer_6
  assign bit_extender_1_out = {{20{controlled_buffer_1_out[11]}}, controlled_buffer_1_out};  // Bit_Extender bit_extender_1
  // Probe on bit_extender_2_out
  assign bit_extender_2_out = {{20{controlled_buffer_3_out[11]}}, controlled_buffer_3_out};  // Bit_Extender bit_extender_2
  assign controlled_buffer_6_out = comparator_4_eq ? 3'b001 : 3'bz;  // Controlled_Buffer controlled_buffer_7
  assign bit_extender_3_out = {{19{controlled_buffer_4_out[12]}}, controlled_buffer_4_out};  // Bit_Extender bit_extender_3
  assign controlled_buffer_6_out = comparator_5_eq ? 3'b010 : 3'bz;  // Controlled_Buffer controlled_buffer_8
  assign controlled_buffer_6_out = comparator_6_eq ? 3'b011 : 3'bz;  // Controlled_Buffer controlled_buffer_9
  assign bit_extender_4_out = {{11{controlled_buffer_2_out[20]}}, controlled_buffer_2_out};  // Bit_Extender bit_extender_4
  assign controlled_buffer_6_out = comparator_7_eq ? 3'b100 : 3'bz;  // Controlled_Buffer controlled_buffer_10
  Multiplexer #(.select(3), .width(32), .enable("false")) multiplexer_1 (
    .in0(bit_extender_1_out), .in1(bit_extender_2_out), .in2(bit_extender_3_out),
    .in3(controlled_buffer_5_out), .in4(bit_extender_4_out), .out(out_3), .sel(controlled_buffer_6_out));  // open: in5, in6, in7

  // Notes on the sheet:
  //   load i-type
  //   alu i-type
  //   jalr i-type
  //   store
  //   SB-type
  //   jal UJ-type
  //   auipc/lui U-type
endmodule
